# Fritzing sketch Headset (saved by Fritzing 0.9.2b)
breadboards: 1

parts:
  U1 = LIPO-2000mAh [package=lipo-2000]
  Part5 = USB LiPoly Charger
  Part1 = LilyPad LiPower
  Part7 = Arduino Pro Mini v13
  microSD1 = MicroSD Breakout
  Part8 = Bluetooth Mate Silver
  CAMERA1 = TTL Serial JPEG Camera
  U2 = AD22100 - Voltage Output Temperature Sensor with Signal Conditioning [part_number=AD22100]

nets:
  N1: U1.+, Part1.B
  GND: U1.-, Part5.GND, Part1.GND, Part7.GND, microSD1.GND, Part8.GND, CAMERA1.GND, U2.GND
  N2: Part5.VBAT, Part1.C
  VCC: Part1.+, Part7.VCC, microSD1.5V, Part8.VCC, CAMERA1.5V, U2.V+
  N3: Part7.D0/TX, Part8.RX_5V
  N4: Part7.D1/RX, Part8.TX_5V
  N5: Part7.D13/SCK, microSD1.CLK
  N6: Part7.D12/MISO, microSD1.DO
  N7: Part7.D11_PWM/MOSI, microSD1.DI
  N8: Part7.D10_PWM/SS, microSD1.CS
  N9: Part7.D7, U2.Vo
  N10: Part7.D6_PWM, CAMERA1.RX
  N11: Part7.D5_PWM, CAMERA1.TX

notes:
  This is actually the pulse sensor
  Connections:
  - black GND
  - red VCC
  - purple Signal

custom parts:
  MicroSD Breakout: 5V-ready microSD Breakout with Level Shifter
  TTL Serial JPEG Camera: TTL Serial JPEG Camera with NTSC Out
